# Fritzing sketch LCD (saved by Fritzing 0.9.1b)
breadboards: 1

parts:
  Part1 = Arduino Uno (Rev3)
  Nokia_5110_LCD_Module1 = Nokia5110LCDModule
  U1 = 74HC595 SMD [package="SO16 [SMD]"]

nets:
  VCC: Part1.3V3, Nokia_5110_LCD_Module1.Vcc, Nokia_5110_LCD_Module1.LED, U1.VCC
  N1: Part1.GND, Nokia_5110_LCD_Module1.Grnd
  N2: Nokia_5110_LCD_Module1.SCLK, U1.Q0

custom parts:
  : Nokia 5110 LCD with 8 pin. It's a 45mm*45mm module part. Description: The Nokia 5110 is a basic graphic LCD screen for lots of applications. It was originally intended for as a cell phone screen. This one is mounted on an easy to solder PCB. It uses the PCD8544 controller. The PCD8544 is a low power CMOS LCD controller/driver, designed to drive a graphic display of 48 rows and 84 columns. All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

// code stored in the sketch: LCD.ino
/*

		This library allows 74hc595 shift registers to be added to digital pins 8, 9 and 10
		Daisy chain to add more shift registers
		Code used under MIT licence
		Original Site: http://bildr.org/2011/02/74hc595/

*/

int SER_Pin = 8;   //pin 14 on the 75HC595
int RCLK_Pin = 9;  //pin 12 on the 75HC595
int SRCLK_Pin = 10; //pin 11 on the 75HC595

//How many of the shift registers - change this
#define number_of_74hc595s 1 

//do not touch
#define numOfRegisterPins number_of_74hc595s * 8

boolean registers[numOfRegisterPins];

void setup(){
  pinMode(SER_Pin, OUTPUT);
  pinMode(RCLK_Pin, OUTPUT);
  pinMode(SRCLK_Pin, OUTPUT);


  //reset all register pins
  clearRegisters();
  writeRegisters();
}               


//set all register pins to LOW
void clearRegisters(){
  for(int i = numOfRegisterPins - 1; i >=  0; i--){
     registers[i] = LOW;
  }
} 


//Set and display registers
//Only call AFTER all values are set how you would like (slow otherwise)
void writeRegisters(){

  digitalWrite(RCLK_Pin, LOW);

  for(int i = numOfRegisterPins - 1; i >=  0; i--){
    digitalWrite(SRCLK_Pin, LOW);

    int val = registers[i];

    digitalWrite(SER_Pin, val);
    digitalWrite(SRCLK_Pin, HIGH);

  }
  digitalWrite(RCLK_Pin, HIGH);

}

//set an individual pin HIGH or LOW
void setRegisterPin(int index, int value){
  registers[index] = value;
}


void loop(){

  setRegisterPin(2, HIGH);
  setRegisterPin(3, HIGH);
  setRegisterPin(4, LOW);
  setRegisterPin(5, HIGH);
  setRegisterPin(7, HIGH);


  writeRegisters();  //MUST BE CALLED TO DISPLAY CHANGES
  //Only call once after the values are set how you need.
}
