# Fritzing sketch DigiTemp (saved by Fritzing 0.9.1b)
breadboards: 1

parts:
  Part1 = Arduino Uno (Rev3)
  R1 = Resistor [tolerance=±5% resistance=4.7k package=THT]
  U1 = TEMPERATURE-SENSOR [package=to-92]

nets:
  GND: Part1.GND, U1.GND
  N1: Part1.D3_PWM, R1.Pin_1, U1.ADJ
  5V: Part1.5V, R1.Pin_0, U1.VCC

// code stored in the sketch: DigiTemp.ino
/*
  Temperature Sensors
 This code will read the temperature from a Dallas 18820 temperature sensor and 
 record the value with a real time.
   
 */

// Temperature sensor libraries
#include <OneWire.h>
#include <DallasTemperature.h>
// Timer libraries
#include <Wire.h>
#include <DS3231.h>

//Bring the in the real time clock functions
DS3231 Clock;
byte year, month, date, DoW, hour, minute, second;
byte ADay, AHour, AMinute, ASecond, ABits;
bool ADy, A12h, Apm;
bool Century=false;

//Setup millisec value
volatile unsigned long millistart;

// Data wire is plugged into data pin 3 on the Arduino
#define ONE_WIRE_BUS 3

//Define an alarm every second and every minute
#define ALRM1_ONCE_PER_SEC  0b1111  // once a second
#define ALRM2_ONCE_PER_MIN  0b111   // once per minute (00 seconds of every minute)
byte ALRM1_SET = ALRM1_ONCE_PER_SEC;
byte ALRM2_SET = ALRM2_ONCE_PER_MIN;

//Define the counting value
volatile unsigned long _millistart;

// Setup a oneWire instance to communicate with any OneWire devices
OneWire oneWire(ONE_WIRE_BUS);
// Pass our oneWire reference to Dallas Temperature. 
DallasTemperature sensors(&oneWire);
// Insert digital thermometer device ID
DeviceAddress digiThermometer = { 0x28, 0xFF, 0xAC, 0x2C, 0x4E, 0x04, 0x00, 0xC6 };

/wSetup the RTC alarm
void setAlarms() {
   
 // Set AlarmBits, ALRM2 first, followed by ALRM1
     int AlarmBits = ALRM2_SET;
     AlarmBits <<= 4;
     AlarmBits |= ALRM1_SET;
     
  // set both alarms to every second
     Clock.setA1Time(Clock.getDoW(), Clock.getHour(h12, PM), Clock.getMinute(), AlarmBits, true, false, false);
     // Turn alarms on
     Clock.turnOnAlarm(1);
}

//Define the second interrupt from the RTC
void SecIntrpt() {
  //Define the chip value of milliseconds at the start of the count
  millistart = millis();
}


// the setup routine runs once when you press reset:
void setup(void) {
  // Start the I2C interface
  Wire.begin();
  // initialize serial communication at 9600 bits per second:
  Serial.begin(9600);
  //start the sensors library
  sensors.begin();
  // set the resolution to 12 bit
  sensors.setResolution(digiThermometer, 12);
  //Set the status of the interrupt pin
  pinMode (2, INPUT);
  //Include an interrupt from the clock
  attachInterrupt(2, SecIntrpt, RISING);
  //Print some intro text
  Serial.println("DS18b20 Temperature Sensor");
  // Get and print the date from the RTC
  Clock.getTime(year, month, date, DoW, hour, minute, second);
  Serial.print(date, DEC);
  Serial.print("/");
  Serial.print(month, DEC);
  Serial.print("/");
  Serial.println(year, DEC);
  setAlarms();
}

void loop() {
  
  //Get the Temperature data from all temperature sensors on the bus1
  sensors.requestTemperatures();
  
  // Get the time
  Clock.getTime(year, month, date, DoW, hour, minute, second);
  int RTCmillisecs = millis() - millistart;
  
  // Print the time and the temperature values
  Serial.print(hour, DEC);
  Serial.print(minute, DEC);
  Serial.print(second, DEC);
  Serial.print(":");
  Serial.println(RTCmillisecs);
  Serial.println(sensors.getTempC(digiThermometer));
}

// code stored in the sketch: Find_ID.ino
// This sketch looks for 1-wire devices and
// prints their addresses (serial number) to
// the UART, in a format that is useful in Arduino sketches
// Tutorial: 
// http://www.hacktronics.com/Tutorials/arduino-1-wire-address-finder.html

#include <OneWire.h>

OneWire  ds(3);  // Connect your 1-wire device to pin 3

void setup(void) {
  Serial.begin(9600);
  discoverOneWireDevices();
}

void discoverOneWireDevices(void) {
  byte i;
  byte present = 0;
  byte data[12];
  byte addr[8];
  
  Serial.print("Looking for 1-Wire devices...\n\r");
  while(ds.search(addr)) {
    Serial.print("\n\rFound \'1-Wire\' device with address:\n\r");
    for( i = 0; i < 8; i++) {
      Serial.print("0x");
      if (addr[i] < 16) {
        Serial.print('0');
      }
      Serial.print(addr[i], HEX);
      if (i < 7) {
        Serial.print(", ");
      }
    }
    if ( OneWire::crc8( addr, 7) != addr[7]) {
        Serial.print("CRC is not valid!\n");
        return;
    }
  }
  Serial.print("\n\r\n\rThat's it.\r\n");
  ds.reset_search();
  return;
}

void loop(void) {
  // nothing to see here
}

// code stored in the sketch: Temp_Simple.ino
#include <OneWire.h>
#include <DallasTemperature.h>

// Data wire is plugged into port 2 on the Arduino
#define ONE_WIRE_BUS 2

// Setup a oneWire instance to communicate with any OneWire devices (not just Maxim/Dallas temperature ICs)
OneWire oneWire(ONE_WIRE_BUS);

// Pass our oneWire reference to Dallas Temperature. 
DallasTemperature sensors(&oneWire);

// arrays to hold device address
DeviceAddress insideThermometer;

void setup(void)
{
  // start serial port
  Serial.begin(9600);
  Serial.println("Dallas Temperature IC Control Library Demo");

  // locate devices on the bus
  Serial.print("Locating devices...");
  sensors.begin();
  Serial.print("Found ");
  Serial.print(sensors.getDeviceCount(), DEC);
  Serial.println(" devices.");

  // report parasite power requirements
  Serial.print("Parasite power is: "); 
  if (sensors.isParasitePowerMode()) Serial.println("ON");
  else Serial.println("OFF");
  
  // assign address manually.  the addresses below will beed to be changed
  // to valid device addresses on your bus.  device address can be retrieved
  // by using either oneWire.search(deviceAddress) or individually via
  // sensors.getAddress(deviceAddress, index)
  //insideThermometer = { 0x28, 0x1D, 0x39, 0x31, 0x2, 0x0, 0x0, 0xF0 };

  // Method 1:
  // search for devices on the bus and assign based on an index.  ideally,
  // you would do this to initially discover addresses on the bus and then 
  // use those addresses and manually assign them (see above) once you know 
  // the devices on your bus (and assuming they don't change).
  if (!sensors.getAddress(insideThermometer, 0)) Serial.println("Unable to find address for Device 0"); 
  
  // method 2: search()
  // search() looks for the next device. Returns 1 if a new address has been
  // returned. A zero might mean that the bus is shorted, there are no devices, 
  // or you have already retrieved all of them.  It might be a good idea to 
  // check the CRC to make sure you didn't get garbage.  The order is 
  // deterministic. You will always get the same devices in the same order
  //
  // Must be called before search()
  //oneWire.reset_search();
  // assigns the first address found to insideThermometer
  //if (!oneWire.search(insideThermometer)) Serial.println("Unable to find address for insideThermometer");

  // show the addresses we found on the bus
  Serial.print("Device 0 Address: ");
  printAddress(insideThermometer);
  Serial.println();

  // set the resolution to 9 bit (Each Dallas/Maxim device is capable of several different resolutions)
  sensors.setResolution(insideThermometer, 9);
 
  Serial.print("Device 0 Resolution: ");
  Serial.print(sensors.getResolution(insideThermometer), DEC); 
  Serial.println();
}

// function to print the temperature for a device
void printTemperature(DeviceAddress deviceAddress)
{
  // method 1 - slower
  //Serial.print("Temp C: ");
  //Serial.print(sensors.getTempC(deviceAddress));
  //Serial.print(" Temp F: ");
  //Serial.print(sensors.getTempF(deviceAddress)); // Makes a second call to getTempC and then converts to Fahrenheit

  // method 2 - faster
  float tempC = sensors.getTempC(deviceAddress);
  Serial.print("Temp C: ");
  Serial.print(tempC);
  Serial.print(" Temp F: ");
  Serial.println(DallasTemperature::toFahrenheit(tempC)); // Converts tempC to Fahrenheit
}

void loop(void)
{ 
  // call sensors.requestTemperatures() to issue a global temperature 
  // request to all devices on the bus
  Serial.print("Requesting temperatures...");
  sensors.requestTemperatures(); // Send the command to get temperatures
  Serial.println("DONE");
  
  // It responds almost immediately. Let's print out the data
  printTemperature(insideThermometer); // Use a simple function to print out the data
}

// function to print a device address
void printAddress(DeviceAddress deviceAddress)
{
  for (uint8_t i = 0; i < 8; i++)
  {
    if (deviceAddress[i] < 16) Serial.print("0");
    Serial.print(deviceAddress[i], HEX);
  }
}
